# Fritzing sketch schematic (saved by Fritzing 0.9.3b)

parts:
  Bauteil2 = Arduino Nano (Rev3.0)
  Bauteil3 = Bluetooth HC-06
  Bauteil1 = HX711 Weighing Sensor Module
  R1 = Resistor [tolerance=±5% resistance=1k package=THT]
  R2 = Resistor [tolerance=±5% resistance=2.2k package=THT]

nets:
  N1: Bauteil2.D1/TX, R1.Pin_1
  N2: Bauteil2.D0/RX, Bauteil3.TXD
  GND: Bauteil2.GND, Bauteil3.GND, Bauteil1.GND, R2.Pin_0
  5V: Bauteil2.5V, Bauteil1.VCC
  N3: Bauteil2.A1, Bauteil1.DO/RX
  N4: Bauteil2.A0, Bauteil1.CK/TX
  3V3: Bauteil2.3V3, Bauteil3.VCC
  N5: Bauteil3.RXD, R1.Pin_0, R2.Pin_1
